// Logisim project Kolache_FP.circ as structural Verilog: 15 circuits, main circuit adder/subtractor
// ADD/SUB
module adder_subtractor (
  input  C_in,
  input  A,
  input  B,
  output OUTPUT,
  output C_out
);

  wire xor_1_out;

  xor xor_1 (xor_1_out, C_in, B);
  Adder #(.width(1)) adder_1 (.a(A), .b(xor_1_out), .out(OUTPUT), .cin(C_in), .cout(C_out));
endmodule

// ADD/SUB
module _32_bit_Adder_subtractor (
  input  in_1,
  input  [31:0] B,
  input  [31:0] A,
  output [31:0] OUTPUT,
  output out_5
);

  wire adder_subtractor_1_c_out, adder_subtractor_2_c_out, adder_subtractor_3_c_out,
       adder_subtractor_4_c_out, adder_subtractor_5_c_out, adder_subtractor_6_c_out,
       adder_subtractor_7_c_out, adder_subtractor_8_c_out, adder_subtractor_9_c_out,
       adder_subtractor_10_c_out, adder_subtractor_11_c_out, adder_subtractor_12_c_out,
       adder_subtractor_13_c_out, adder_subtractor_14_c_out, adder_subtractor_15_c_out,
       adder_subtractor_16_c_out, adder_subtractor_17_c_out, adder_subtractor_18_c_out,
       adder_subtractor_19_c_out, adder_subtractor_20_c_out, adder_subtractor_21_c_out,
       adder_subtractor_22_c_out, adder_subtractor_23_c_out, adder_subtractor_24_c_out,
       adder_subtractor_25_c_out, adder_subtractor_26_c_out, adder_subtractor_27_c_out,
       adder_subtractor_28_c_out, adder_subtractor_29_c_out, adder_subtractor_30_c_out,
       adder_subtractor_31_c_out;

  adder_subtractor adder_subtractor_1 (
    .C_in(in_1), .A(A[0]), .B(B[1]), .OUTPUT(OUTPUT[0]), .C_out(adder_subtractor_1_c_out));
  adder_subtractor adder_subtractor_2 (
    .C_in(adder_subtractor_1_c_out), .A(A[1]), .B(B[1]), .OUTPUT(OUTPUT[1]), .C_out(adder_subtractor_2_c_out));
  adder_subtractor adder_subtractor_3 (
    .C_in(adder_subtractor_2_c_out), .A(A[2]), .B(B[2]), .OUTPUT(OUTPUT[2]), .C_out(adder_subtractor_3_c_out));
  adder_subtractor adder_subtractor_4 (
    .C_in(adder_subtractor_3_c_out), .A(A[3]), .B(B[3]), .OUTPUT(OUTPUT[3]), .C_out(adder_subtractor_4_c_out));
  adder_subtractor adder_subtractor_5 (
    .C_in(adder_subtractor_4_c_out), .A(A[4]), .B(B[4]), .OUTPUT(OUTPUT[4]), .C_out(adder_subtractor_5_c_out));
  adder_subtractor adder_subtractor_6 (
    .C_in(adder_subtractor_5_c_out), .A(A[5]), .B(B[5]), .OUTPUT(OUTPUT[5]), .C_out(adder_subtractor_6_c_out));
  adder_subtractor adder_subtractor_7 (
    .C_in(adder_subtractor_6_c_out), .A(A[6]), .B(B[6]), .OUTPUT(OUTPUT[6]), .C_out(adder_subtractor_7_c_out));
  adder_subtractor adder_subtractor_8 (
    .C_in(adder_subtractor_7_c_out), .A(A[7]), .B(B[7]), .OUTPUT(OUTPUT[7]), .C_out(adder_subtractor_8_c_out));
  adder_subtractor adder_subtractor_9 (
    .C_in(adder_subtractor_8_c_out), .A(A[8]), .B(B[8]), .OUTPUT(OUTPUT[8]), .C_out(adder_subtractor_9_c_out));
  adder_subtractor adder_subtractor_10 (
    .C_in(adder_subtractor_9_c_out), .A(A[9]), .B(B[9]), .OUTPUT(OUTPUT[9]), .C_out(adder_subtractor_10_c_out));
  adder_subtractor adder_subtractor_11 (
    .C_in(adder_subtractor_10_c_out), .A(A[10]), .B(B[10]), .OUTPUT(OUTPUT[10]),
    .C_out(adder_subtractor_11_c_out));
  adder_subtractor adder_subtractor_12 (
    .C_in(adder_subtractor_11_c_out), .A(A[11]), .B(B[11]), .OUTPUT(OUTPUT[11]),
    .C_out(adder_subtractor_12_c_out));
  adder_subtractor adder_subtractor_13 (
    .C_in(adder_subtractor_12_c_out), .A(A[12]), .B(B[12]), .OUTPUT(OUTPUT[12]),
    .C_out(adder_subtractor_13_c_out));
  adder_subtractor adder_subtractor_14 (
    .C_in(adder_subtractor_13_c_out), .A(A[13]), .B(B[13]), .OUTPUT(OUTPUT[13]),
    .C_out(adder_subtractor_14_c_out));
  adder_subtractor adder_subtractor_15 (
    .C_in(adder_subtractor_14_c_out), .A(A[14]), .B(B[14]), .OUTPUT(OUTPUT[14]),
    .C_out(adder_subtractor_15_c_out));
  adder_subtractor adder_subtractor_16 (
    .C_in(adder_subtractor_15_c_out), .A(A[15]), .B(B[15]), .OUTPUT(OUTPUT[15]),
    .C_out(adder_subtractor_16_c_out));
  adder_subtractor adder_subtractor_17 (
    .C_in(adder_subtractor_16_c_out), .A(A[16]), .B(B[16]), .OUTPUT(OUTPUT[16]),
    .C_out(adder_subtractor_17_c_out));
  adder_subtractor adder_subtractor_18 (
    .C_in(adder_subtractor_17_c_out), .A(A[17]), .B(B[17]), .OUTPUT(OUTPUT[17]),
    .C_out(adder_subtractor_18_c_out));
  adder_subtractor adder_subtractor_19 (
    .C_in(adder_subtractor_18_c_out), .A(A[18]), .B(B[18]), .OUTPUT(OUTPUT[18]),
    .C_out(adder_subtractor_19_c_out));
  adder_subtractor adder_subtractor_20 (
    .C_in(adder_subtractor_19_c_out), .A(A[19]), .B(B[19]), .OUTPUT(OUTPUT[19]),
    .C_out(adder_subtractor_20_c_out));
  adder_subtractor adder_subtractor_21 (
    .C_in(adder_subtractor_20_c_out), .A(A[20]), .B(B[20]), .OUTPUT(OUTPUT[20]),
    .C_out(adder_subtractor_21_c_out));
  adder_subtractor adder_subtractor_22 (
    .C_in(adder_subtractor_21_c_out), .A(A[21]), .B(B[21]), .OUTPUT(OUTPUT[21]),
    .C_out(adder_subtractor_22_c_out));
  adder_subtractor adder_subtractor_23 (
    .C_in(adder_subtractor_22_c_out), .A(A[22]), .B(B[22]), .OUTPUT(OUTPUT[22]),
    .C_out(adder_subtractor_23_c_out));
  adder_subtractor adder_subtractor_24 (
    .C_in(adder_subtractor_23_c_out), .A(A[23]), .B(B[23]), .OUTPUT(OUTPUT[23]),
    .C_out(adder_subtractor_24_c_out));
  adder_subtractor adder_subtractor_25 (
    .C_in(adder_subtractor_24_c_out), .A(A[24]), .B(B[24]), .OUTPUT(OUTPUT[24]),
    .C_out(adder_subtractor_25_c_out));
  adder_subtractor adder_subtractor_26 (
    .C_in(adder_subtractor_25_c_out), .A(A[25]), .B(B[25]), .OUTPUT(OUTPUT[25]),
    .C_out(adder_subtractor_26_c_out));
  adder_subtractor adder_subtractor_27 (
    .C_in(adder_subtractor_26_c_out), .A(A[26]), .B(B[26]), .OUTPUT(OUTPUT[26]),
    .C_out(adder_subtractor_27_c_out));
  adder_subtractor adder_subtractor_28 (
    .C_in(adder_subtractor_27_c_out), .A(A[27]), .B(B[27]), .OUTPUT(OUTPUT[27]),
    .C_out(adder_subtractor_28_c_out));
  adder_subtractor adder_subtractor_29 (
    .C_in(adder_subtractor_28_c_out), .A(A[28]), .B(B[28]), .OUTPUT(OUTPUT[28]),
    .C_out(adder_subtractor_29_c_out));
  adder_subtractor adder_subtractor_30 (
    .C_in(adder_subtractor_29_c_out), .A(A[29]), .B(B[29]), .OUTPUT(OUTPUT[29]),
    .C_out(adder_subtractor_30_c_out));
  adder_subtractor adder_subtractor_31 (
    .C_in(adder_subtractor_30_c_out), .A(A[30]), .B(B[30]), .OUTPUT(OUTPUT[30]),
    .C_out(adder_subtractor_31_c_out));
  adder_subtractor adder_subtractor_32 (
    .C_in(adder_subtractor_31_c_out), .A(A[31]), .B(B[31]), .OUTPUT(OUTPUT[31]), .C_out(out_5));

  assign B[0] = B[1];

  // Other names for the same wires on the sheet: B0 = B[1]; S0 = OUTPUT[0]; S1 = OUTPUT[1]; S2 = OUTPUT[2];
  //   S3 = OUTPUT[3]; S4 = OUTPUT[4]; S5 = OUTPUT[5]; S6 = OUTPUT[6]; S7 = OUTPUT[7]; S8 = OUTPUT[8]; S9 = OUTPUT[9];
  //   S10 = OUTPUT[10]; S11 = OUTPUT[11]; S12 = OUTPUT[12]; S13 = OUTPUT[13]; S14 = OUTPUT[14]; S15 = OUTPUT[15];
  //   S16 = OUTPUT[16]; S17 = OUTPUT[17]; S18 = OUTPUT[18]; S19 = OUTPUT[19]; S20 = OUTPUT[20]; S21 = OUTPUT[21];
  //   S22 = OUTPUT[22]; S23 = OUTPUT[23]; S24 = OUTPUT[24]; S25 = OUTPUT[25]; S26 = OUTPUT[26]; S27 = OUTPUT[27];
  //   S28 = OUTPUT[28]; S29 = OUTPUT[29]; S30 = OUTPUT[30]; S31 = OUTPUT[31]
endmodule

module AND (
  input  A,
  input  B,
  output OUTPUT
);

  and and_1 (OUTPUT, A, B);
endmodule

// AND
module _32_bit_AND (
  input  [31:0] B,
  input  [31:0] A,
  output [31:0] out_3
);

  AND and_1 (.A(A[0]), .B(B[0]), .OUTPUT(out_3[0]));
  AND and_2 (.A(A[1]), .B(B[1]), .OUTPUT(out_3[1]));
  AND and_3 (.A(A[2]), .B(B[2]), .OUTPUT(out_3[2]));
  AND and_4 (.A(A[3]), .B(B[3]), .OUTPUT(out_3[3]));
  AND and_5 (.A(A[4]), .B(B[4]), .OUTPUT(out_3[4]));
  AND and_6 (.A(A[5]), .B(B[5]), .OUTPUT(out_3[5]));
  AND and_7 (.A(A[6]), .B(B[6]), .OUTPUT(out_3[6]));
  AND and_8 (.A(A[7]), .B(B[7]), .OUTPUT(out_3[7]));
  AND and_9 (.A(A[8]), .B(B[8]), .OUTPUT(out_3[8]));
  AND and_10 (.A(A[9]), .B(B[9]), .OUTPUT(out_3[9]));
  AND and_11 (.A(A[10]), .B(B[10]), .OUTPUT(out_3[10]));
  AND and_12 (.A(A[11]), .B(B[11]), .OUTPUT(out_3[11]));
  AND and_13 (.A(A[12]), .B(B[12]), .OUTPUT(out_3[12]));
  AND and_14 (.A(A[13]), .B(B[13]), .OUTPUT(out_3[13]));
  AND and_15 (.A(A[14]), .B(B[14]), .OUTPUT(out_3[14]));
  AND and_16 (.A(A[15]), .B(B[15]), .OUTPUT(out_3[15]));
  AND and_17 (.A(A[16]), .B(B[16]), .OUTPUT(out_3[16]));
  AND and_18 (.A(A[17]), .B(B[17]), .OUTPUT(out_3[17]));
  AND and_19 (.A(A[18]), .B(B[18]), .OUTPUT(out_3[18]));
  AND and_20 (.A(A[19]), .B(B[19]), .OUTPUT(out_3[19]));
  AND and_21 (.A(A[20]), .B(B[20]), .OUTPUT(out_3[20]));
  AND and_22 (.A(A[21]), .B(B[21]), .OUTPUT(out_3[21]));
  AND and_23 (.A(A[22]), .B(B[22]), .OUTPUT(out_3[22]));
  AND and_24 (.A(A[23]), .B(B[23]), .OUTPUT(out_3[23]));
  AND and_25 (.A(A[24]), .B(B[24]), .OUTPUT(out_3[24]));
  AND and_26 (.A(A[25]), .B(B[25]), .OUTPUT(out_3[25]));
  AND and_27 (.A(A[26]), .B(B[26]), .OUTPUT(out_3[26]));
  AND and_28 (.A(A[27]), .B(B[27]), .OUTPUT(out_3[27]));
  AND and_29 (.A(A[28]), .B(B[28]), .OUTPUT(out_3[28]));
  AND and_30 (.A(A[29]), .B(B[29]), .OUTPUT(out_3[29]));
  AND and_31 (.A(A[30]), .B(B[30]), .OUTPUT(out_3[30]));
  AND and_32 (.A(A[31]), .B(B[31]), .OUTPUT(out_3[31]));

  // Other names for the same wires on the sheet: S0 = out_3[0]; S1 = out_3[1]; S2 = out_3[2]; S3 = out_3[3];
  //   S4 = out_3[4]; S5 = out_3[5]; S6 = out_3[6]; S7 = out_3[7]; S8 = out_3[8]; S9 = out_3[9]; S10 = out_3[10];
  //   S11 = out_3[11]; S12 = out_3[12]; S13 = out_3[13]; S14 = out_3[14]; S15 = out_3[15]; S16 = out_3[16];
  //   S17 = out_3[17]; S18 = out_3[18]; S19 = out_3[19]; S20 = out_3[20]; S21 = out_3[21]; S22 = out_3[22];
  //   S23 = out_3[23]; S24 = out_3[24]; S25 = out_3[25]; S26 = out_3[26]; S27 = out_3[27]; S28 = out_3[28];
  //   S29 = out_3[29]; S30 = out_3[30]; S31 = out_3[31]
endmodule

module OR (
  input  A,
  input  B,
  output OUTPUT
);

  or or_1 (OUTPUT, A, B);
endmodule

// OR
module _32_bit_OR (
  input  [31:0] A,
  input  [31:0] B,
  output [31:0] OUTPUT
);

  OR or_1 (.A(A[0]), .OUTPUT(OUTPUT[0]), .B(B[0]));
  OR or_2 (.A(A[1]), .OUTPUT(OUTPUT[1]), .B(B[1]));
  OR or_3 (.A(A[2]), .OUTPUT(OUTPUT[2]), .B(B[2]));
  OR or_4 (.A(A[3]), .OUTPUT(OUTPUT[3]), .B(B[3]));
  OR or_5 (.A(A[4]), .OUTPUT(OUTPUT[4]), .B(B[4]));
  OR or_6 (.A(A[5]), .OUTPUT(OUTPUT[5]), .B(B[5]));
  OR or_7 (.A(A[6]), .OUTPUT(OUTPUT[6]), .B(B[6]));
  OR or_8 (.A(A[7]), .OUTPUT(OUTPUT[7]), .B(B[7]));
  OR or_9 (.A(A[8]), .OUTPUT(OUTPUT[8]), .B(B[8]));
  OR or_10 (.A(A[9]), .OUTPUT(OUTPUT[9]), .B(B[9]));
  OR or_11 (.A(A[10]), .OUTPUT(OUTPUT[10]), .B(B[10]));
  OR or_12 (.A(A[11]), .OUTPUT(OUTPUT[11]), .B(B[11]));
  OR or_13 (.A(A[12]), .OUTPUT(OUTPUT[12]), .B(B[12]));
  OR or_14 (.A(A[13]), .OUTPUT(OUTPUT[13]), .B(B[13]));
  OR or_15 (.A(A[14]), .OUTPUT(OUTPUT[14]), .B(B[14]));
  OR or_16 (.A(A[15]), .OUTPUT(OUTPUT[15]), .B(B[15]));
  OR or_17 (.A(A[16]), .OUTPUT(OUTPUT[16]), .B(B[16]));
  OR or_18 (.A(A[17]), .OUTPUT(OUTPUT[17]), .B(B[17]));
  OR or_19 (.A(A[18]), .OUTPUT(OUTPUT[18]), .B(B[18]));
  OR or_20 (.A(A[19]), .OUTPUT(OUTPUT[19]), .B(B[19]));
  OR or_21 (.A(A[20]), .OUTPUT(OUTPUT[20]), .B(B[20]));
  OR or_22 (.A(A[21]), .OUTPUT(OUTPUT[21]), .B(B[21]));
  OR or_23 (.A(A[22]), .OUTPUT(OUTPUT[22]), .B(B[22]));
  OR or_24 (.A(A[23]), .OUTPUT(OUTPUT[23]), .B(B[23]));
  OR or_25 (.A(A[24]), .OUTPUT(OUTPUT[24]), .B(B[24]));
  OR or_26 (.A(A[25]), .OUTPUT(OUTPUT[25]), .B(B[25]));
  OR or_27 (.A(A[26]), .OUTPUT(OUTPUT[26]), .B(B[26]));
  OR or_28 (.A(A[27]), .OUTPUT(OUTPUT[27]), .B(B[27]));
  OR or_29 (.A(A[28]), .OUTPUT(OUTPUT[28]), .B(B[28]));
  OR or_30 (.A(A[29]), .OUTPUT(OUTPUT[29]), .B(B[29]));
  OR or_31 (.A(A[30]), .OUTPUT(OUTPUT[30]), .B(B[30]));
  OR or_32 (.A(A[31]), .OUTPUT(OUTPUT[31]), .B(B[31]));

  // Other names for the same wires on the sheet: S0 = OUTPUT[0]; S1 = OUTPUT[1]; S2 = OUTPUT[2]; S3 = OUTPUT[3];
  //   S4 = OUTPUT[4]; S5 = OUTPUT[5]; S6 = OUTPUT[6]; S7 = OUTPUT[7]; S8 = OUTPUT[8]; S9 = OUTPUT[9];
  //   S10 = OUTPUT[10]; S11 = OUTPUT[11]; S12 = OUTPUT[12]; S13 = OUTPUT[13]; S14 = OUTPUT[14]; S15 = OUTPUT[15];
  //   S16 = OUTPUT[16]; S17 = OUTPUT[17]; S18 = OUTPUT[18]; S19 = OUTPUT[19]; S20 = OUTPUT[20]; S21 = OUTPUT[21];
  //   S22 = OUTPUT[22]; S23 = OUTPUT[23]; S24 = OUTPUT[24]; S25 = OUTPUT[25]; S26 = OUTPUT[26]; S27 = OUTPUT[27];
  //   S28 = OUTPUT[28]; S29 = OUTPUT[29]; S30 = OUTPUT[30]; S31 = OUTPUT[31]
endmodule

module NOT (
  input  A,
  output OUTPUT
);

  not not_1 (OUTPUT, A);
endmodule

// NOT
module _32_bit_NOT (
  input  [31:0] A,
  output [31:0] out_2
);

  NOT not_1 (.A(A[0]), .OUTPUT(out_2[0]));
  NOT not_2 (.A(A[2]), .OUTPUT(out_2[2]));
  NOT not_3 (.A(A[4]), .OUTPUT(out_2[4]));
  NOT not_4 (.A(A[6]), .OUTPUT(out_2[6]));
  NOT not_5 (.A(A[8]), .OUTPUT(out_2[8]));
  NOT not_6 (.A(A[10]), .OUTPUT(out_2[10]));
  NOT not_7 (.A(A[12]), .OUTPUT(out_2[12]));
  NOT not_8 (.A(A[14]), .OUTPUT(out_2[14]));
  NOT not_9 (.A(A[16]), .OUTPUT(out_2[16]));
  NOT not_10 (.A(A[18]), .OUTPUT(out_2[18]));
  NOT not_11 (.A(A[20]), .OUTPUT(out_2[20]));
  NOT not_12 (.A(A[22]), .OUTPUT(out_2[22]));
  NOT not_13 (.A(A[24]), .OUTPUT(out_2[24]));
  NOT not_14 (.A(A[26]), .OUTPUT(out_2[26]));
  NOT not_15 (.A(A[28]), .OUTPUT(out_2[28]));
  NOT not_16 (.A(A[30]), .OUTPUT(out_2[30]));
  NOT not_17 (.A(A[1]), .OUTPUT(out_2[1]));
  NOT not_18 (.A(A[3]), .OUTPUT(out_2[3]));
  NOT not_19 (.A(A[5]), .OUTPUT(out_2[5]));
  NOT not_20 (.A(A[7]), .OUTPUT(out_2[7]));
  NOT not_21 (.A(A[9]), .OUTPUT(out_2[9]));
  NOT not_22 (.A(A[11]), .OUTPUT(out_2[11]));
  NOT not_23 (.A(A[13]), .OUTPUT(out_2[13]));
  NOT not_24 (.A(A[15]), .OUTPUT(out_2[15]));
  NOT not_25 (.A(A[17]), .OUTPUT(out_2[17]));
  NOT not_26 (.A(A[19]), .OUTPUT(out_2[19]));
  NOT not_27 (.A(A[21]), .OUTPUT(out_2[21]));
  NOT not_28 (.A(A[23]), .OUTPUT(out_2[23]));
  NOT not_29 (.A(A[25]), .OUTPUT(out_2[25]));
  NOT not_30 (.A(A[27]), .OUTPUT(out_2[27]));
  NOT not_31 (.A(A[29]), .OUTPUT(out_2[29]));
  NOT not_32 (.A(A[31]), .OUTPUT(out_2[31]));
endmodule

// Greater
module Greater_Than (
  input  A,
  input  B,
  output OUTPUT
);

  wire not_1_out;

  not not_1 (not_1_out, B);
  and and_1 (OUTPUT, A, not_1_out);
endmodule

// GREATER
module _32_bit_Greater_than (
  input  [31:0] Output,
  input  [31:0] A,
  input  [31:0] B
);

  Greater_Than greater_than_1 (.A(A[0]), .B(B[0]), .OUTPUT(Output[0]));
  Greater_Than greater_than_2 (.A(A[1]), .B(B[1]), .OUTPUT(Output[1]));
  Greater_Than greater_than_3 (.A(A[2]), .B(B[2]), .OUTPUT(Output[2]));
  Greater_Than greater_than_4 (.A(A[3]), .B(B[3]), .OUTPUT(Output[3]));
  Greater_Than greater_than_5 (.A(A[4]), .B(B[4]), .OUTPUT(Output[4]));
  Greater_Than greater_than_6 (.A(A[5]), .B(B[5]), .OUTPUT(Output[5]));
  Greater_Than greater_than_7 (.A(A[6]), .B(B[6]), .OUTPUT(Output[6]));
  Greater_Than greater_than_8 (.A(A[7]), .B(B[7]), .OUTPUT(Output[7]));
  Greater_Than greater_than_9 (.A(A[8]), .B(B[8]), .OUTPUT(Output[8]));
  Greater_Than greater_than_10 (.A(A[9]), .B(B[9]), .OUTPUT(Output[9]));
  Greater_Than greater_than_11 (.A(A[10]), .B(B[10]), .OUTPUT(Output[10]));
  Greater_Than greater_than_12 (.A(A[11]), .B(B[11]), .OUTPUT(Output[11]));
  Greater_Than greater_than_13 (.A(A[12]), .B(B[12]), .OUTPUT(Output[12]));
  Greater_Than greater_than_14 (.A(A[13]), .B(B[13]), .OUTPUT(Output[13]));
  Greater_Than greater_than_15 (.A(A[14]), .B(B[14]), .OUTPUT(Output[14]));
  Greater_Than greater_than_16 (.A(A[15]), .B(B[15]), .OUTPUT(Output[15]));
  Greater_Than greater_than_17 (.A(A[16]), .B(B[16]), .OUTPUT(Output[16]));
  Greater_Than greater_than_18 (.A(A[17]), .B(B[17]), .OUTPUT(Output[17]));
  Greater_Than greater_than_19 (.A(A[18]), .B(B[18]), .OUTPUT(Output[18]));
  Greater_Than greater_than_20 (.A(A[19]), .B(B[19]), .OUTPUT(Output[19]));
  Greater_Than greater_than_21 (.A(A[20]), .B(B[20]), .OUTPUT(Output[20]));
  Greater_Than greater_than_22 (.A(A[21]), .B(B[21]), .OUTPUT(Output[21]));
  Greater_Than greater_than_23 (.A(A[22]), .B(B[22]), .OUTPUT(Output[22]));
  Greater_Than greater_than_24 (.A(A[23]), .B(B[23]), .OUTPUT(Output[23]));
  Greater_Than greater_than_25 (.A(A[24]), .B(B[24]), .OUTPUT(Output[24]));
  Greater_Than greater_than_26 (.A(A[25]), .B(B[25]), .OUTPUT(Output[25]));
  Greater_Than greater_than_27 (.A(A[26]), .B(B[26]), .OUTPUT(Output[26]));
  Greater_Than greater_than_28 (.A(A[27]), .B(B[27]), .OUTPUT(Output[27]));
  Greater_Than greater_than_29 (.A(A[28]), .B(B[28]), .OUTPUT(Output[28]));
  Greater_Than greater_than_30 (.A(A[29]), .B(B[29]), .OUTPUT(Output[29]));
  Greater_Than greater_than_31 (.A(A[30]), .B(B[30]), .OUTPUT(Output[30]));
  Greater_Than greater_than_32 (.A(A[31]), .B(B[31]), .OUTPUT(Output[31]));
endmodule

module Equal_To (
  input  A,
  input  B,
  output OUTPUT
);

  wire xor_1_out;

  xor xor_1 (xor_1_out, A, B);
  not not_1 (OUTPUT, xor_1_out);
endmodule

// EQUAL
module _32_bit_equal_to (
  input  [31:0] A,
  input  [31:0] B,
  output out_3
);

  wire equal_to_1_output, equal_to_2_output, equal_to_3_output, equal_to_4_output, equal_to_5_output,
       equal_to_6_output, equal_to_7_output, equal_to_8_output, equal_to_9_output, equal_to_10_output,
       equal_to_11_output, equal_to_12_output, equal_to_13_output, equal_to_14_output, equal_to_15_output,
       equal_to_16_output, equal_to_17_output, equal_to_18_output, equal_to_19_output, equal_to_20_output,
       equal_to_21_output, equal_to_22_output, equal_to_23_output, equal_to_24_output, equal_to_25_output,
       equal_to_26_output, equal_to_27_output, equal_to_28_output, equal_to_29_output, equal_to_30_output,
       equal_to_31_output, equal_to_32_output;

  Equal_To equal_to_1 (.A(A[0]), .B(B[0]), .OUTPUT(equal_to_1_output));
  Equal_To equal_to_2 (.A(A[1]), .B(B[1]), .OUTPUT(equal_to_2_output));
  Equal_To equal_to_3 (.A(A[2]), .B(B[2]), .OUTPUT(equal_to_3_output));
  Equal_To equal_to_4 (.A(A[3]), .B(B[3]), .OUTPUT(equal_to_4_output));
  Equal_To equal_to_5 (.A(A[4]), .B(B[4]), .OUTPUT(equal_to_5_output));
  Equal_To equal_to_6 (.A(A[5]), .B(B[5]), .OUTPUT(equal_to_6_output));
  Equal_To equal_to_7 (.A(A[6]), .B(B[6]), .OUTPUT(equal_to_7_output));
  Equal_To equal_to_8 (.A(A[7]), .B(B[7]), .OUTPUT(equal_to_8_output));
  Equal_To equal_to_9 (.A(A[8]), .B(B[8]), .OUTPUT(equal_to_9_output));
  Equal_To equal_to_10 (.A(A[9]), .B(B[9]), .OUTPUT(equal_to_10_output));
  Equal_To equal_to_11 (.A(A[10]), .B(B[10]), .OUTPUT(equal_to_11_output));
  Equal_To equal_to_12 (.A(A[11]), .B(B[11]), .OUTPUT(equal_to_12_output));
  Equal_To equal_to_13 (.A(A[12]), .B(B[12]), .OUTPUT(equal_to_13_output));
  Equal_To equal_to_14 (.A(A[13]), .B(B[13]), .OUTPUT(equal_to_14_output));
  Equal_To equal_to_15 (.A(A[14]), .B(B[14]), .OUTPUT(equal_to_15_output));
  Equal_To equal_to_16 (.A(A[15]), .B(B[15]), .OUTPUT(equal_to_16_output));
  Equal_To equal_to_17 (.A(A[16]), .B(B[16]), .OUTPUT(equal_to_17_output));
  Equal_To equal_to_18 (.A(A[17]), .B(B[17]), .OUTPUT(equal_to_18_output));
  Equal_To equal_to_19 (.A(A[18]), .B(B[18]), .OUTPUT(equal_to_19_output));
  Equal_To equal_to_20 (.A(A[19]), .B(B[19]), .OUTPUT(equal_to_20_output));
  Equal_To equal_to_21 (.A(A[20]), .B(B[20]), .OUTPUT(equal_to_21_output));
  Equal_To equal_to_22 (.A(A[21]), .B(B[21]), .OUTPUT(equal_to_22_output));
  Equal_To equal_to_23 (.A(A[22]), .B(B[22]), .OUTPUT(equal_to_23_output));
  Equal_To equal_to_24 (.A(A[23]), .B(B[23]), .OUTPUT(equal_to_24_output));
  Equal_To equal_to_25 (.A(A[24]), .B(B[24]), .OUTPUT(equal_to_25_output));
  Equal_To equal_to_26 (.A(A[25]), .B(B[25]), .OUTPUT(equal_to_26_output));
  Equal_To equal_to_27 (.A(A[26]), .B(B[26]), .OUTPUT(equal_to_27_output));
  Equal_To equal_to_28 (.A(A[27]), .B(B[27]), .OUTPUT(equal_to_28_output));
  Equal_To equal_to_29 (.A(A[28]), .B(B[28]), .OUTPUT(equal_to_29_output));
  Equal_To equal_to_30 (.A(A[29]), .B(B[29]), .OUTPUT(equal_to_30_output));
  Equal_To equal_to_31 (.A(A[30]), .B(B[30]), .OUTPUT(equal_to_31_output));
  Equal_To equal_to_32 (.A(A[31]), .B(B[31]), .OUTPUT(equal_to_32_output));
  and and_1 (out_3, equal_to_1_output, equal_to_2_output, equal_to_3_output, equal_to_4_output, equal_to_5_output, equal_to_6_output, equal_to_7_output, equal_to_8_output, equal_to_9_output, equal_to_10_output, equal_to_11_output, equal_to_12_output, equal_to_13_output, equal_to_14_output, equal_to_15_output, equal_to_16_output, equal_to_18_output, equal_to_19_output, equal_to_20_output, equal_to_21_output, equal_to_22_output, equal_to_23_output, equal_to_24_output, equal_to_25_output, equal_to_26_output, equal_to_27_output, equal_to_28_output, equal_to_29_output, equal_to_30_output, equal_to_31_output, equal_to_32_output, equal_to_17_output);
endmodule

// LESS
module Less_than (
  input  A,
  input  B,
  output OUTPUT
);

  wire not_1_out;

  not not_1 (not_1_out, A);
  and and_1 (OUTPUT, not_1_out, B);
endmodule

// LESS
module _32_bit_Less_than (
  input  [31:0] A,
  input  [31:0] B,
  output out_3
);

  wire less_than_1_output, less_than_2_output, less_than_3_output, less_than_4_output, less_than_5_output,
       less_than_6_output, less_than_7_output, less_than_8_output, less_than_9_output, less_than_10_output,
       less_than_11_output, less_than_12_output, less_than_13_output, less_than_14_output,
       less_than_15_output, less_than_16_output, less_than_17_output, less_than_18_output,
       less_than_19_output, less_than_20_output, less_than_21_output, less_than_22_output,
       less_than_23_output, less_than_24_output, less_than_25_output, less_than_26_output,
       less_than_27_output, less_than_28_output, less_than_29_output, less_than_30_output,
       less_than_31_output, less_than_32_output;

  Less_than less_than_1 (.A(A[0]), .B(B[0]), .OUTPUT(less_than_1_output));
  Less_than less_than_2 (.A(A[1]), .B(B[1]), .OUTPUT(less_than_2_output));
  Less_than less_than_3 (.A(A[2]), .B(B[2]), .OUTPUT(less_than_3_output));
  Less_than less_than_4 (.A(A[3]), .B(B[3]), .OUTPUT(less_than_4_output));
  Less_than less_than_5 (.A(A[4]), .B(B[4]), .OUTPUT(less_than_5_output));
  Less_than less_than_6 (.A(A[5]), .B(B[5]), .OUTPUT(less_than_6_output));
  Less_than less_than_7 (.A(A[6]), .B(B[6]), .OUTPUT(less_than_7_output));
  Less_than less_than_8 (.A(A[7]), .B(B[7]), .OUTPUT(less_than_8_output));
  Less_than less_than_9 (.A(A[8]), .B(B[8]), .OUTPUT(less_than_9_output));
  Less_than less_than_10 (.A(A[9]), .B(B[9]), .OUTPUT(less_than_10_output));
  Less_than less_than_11 (.A(A[10]), .B(B[10]), .OUTPUT(less_than_11_output));
  Less_than less_than_12 (.A(A[11]), .B(B[11]), .OUTPUT(less_than_12_output));
  Less_than less_than_13 (.A(A[12]), .B(B[12]), .OUTPUT(less_than_13_output));
  Less_than less_than_14 (.A(A[13]), .B(B[13]), .OUTPUT(less_than_14_output));
  Less_than less_than_15 (.A(A[14]), .B(B[14]), .OUTPUT(less_than_15_output));
  Less_than less_than_16 (.A(A[15]), .B(B[15]), .OUTPUT(less_than_16_output));
  Less_than less_than_17 (.A(A[16]), .B(B[16]), .OUTPUT(less_than_17_output));
  Less_than less_than_18 (.A(A[17]), .B(B[17]), .OUTPUT(less_than_18_output));
  Less_than less_than_19 (.A(A[18]), .B(B[18]), .OUTPUT(less_than_19_output));
  Less_than less_than_20 (.A(A[19]), .B(B[19]), .OUTPUT(less_than_20_output));
  Less_than less_than_21 (.A(A[20]), .B(B[20]), .OUTPUT(less_than_21_output));
  Less_than less_than_22 (.A(A[21]), .B(B[21]), .OUTPUT(less_than_22_output));
  Less_than less_than_23 (.A(A[22]), .B(B[22]), .OUTPUT(less_than_23_output));
  Less_than less_than_24 (.A(A[23]), .B(B[23]), .OUTPUT(less_than_24_output));
  Less_than less_than_25 (.A(A[24]), .B(B[24]), .OUTPUT(less_than_25_output));
  Less_than less_than_26 (.A(A[25]), .B(B[25]), .OUTPUT(less_than_26_output));
  Less_than less_than_27 (.A(A[26]), .B(B[26]), .OUTPUT(less_than_27_output));
  Less_than less_than_28 (.A(A[27]), .B(B[27]), .OUTPUT(less_than_28_output));
  Less_than less_than_29 (.A(A[28]), .B(B[28]), .OUTPUT(less_than_29_output));
  Less_than less_than_30 (.A(A[29]), .B(B[29]), .OUTPUT(less_than_30_output));
  Less_than less_than_31 (.A(A[30]), .B(B[30]), .OUTPUT(less_than_31_output));
  Less_than less_than_32 (.A(A[31]), .B(B[31]), .OUTPUT(less_than_32_output));
  or or_1 (out_3, less_than_16_output, less_than_1_output, less_than_2_output, less_than_3_output, less_than_4_output, less_than_5_output, less_than_6_output, less_than_7_output, less_than_8_output, less_than_9_output, less_than_10_output, less_than_11_output, less_than_12_output, less_than_13_output, less_than_14_output, less_than_15_output, less_than_17_output, less_than_18_output, less_than_19_output, less_than_20_output, less_than_21_output, less_than_22_output, less_than_23_output, less_than_24_output, less_than_25_output, less_than_26_output, less_than_27_output, less_than_28_output, less_than_29_output, less_than_30_output, less_than_31_output, less_than_32_output);
endmodule

module _32_bit_ALU (
  input  [31:0] A,
  input  [31:0] B,
  input  clr,
  input  clk,
  input  [3:0] OpCode,
  input  CarryIn,
  output [31:0] OUTPUT,
  output Overflow,
  output CarryOut
);

  wire [31:0] and_1_out, comparator_1_eq, comparator_1_gt, comparator_1_lt, multiplexer_1_out,
       n32_bit_adder_subtractor_1_output, or_1_out;

  assign and_1_out = A & B;  // AND_Gate and_1, 32 bits wide
  assign or_1_out = A | B;  // OR_Gate or_1, 32 bits wide
  _32_bit_Adder_subtractor u_32_bit_adder_subtractor_1 (
    .B(B), .A(A), .OUTPUT(n32_bit_adder_subtractor_1_output), .in_1(CarryIn), .out_5(CarryOut));
  Comparator #(.width(32)) comparator_1 (
    .a(A), .b(B), .gt(comparator_1_gt[0]), .eq(comparator_1_eq[0]), .lt(comparator_1_lt[0]));
  xor xor_1 (Overflow, CarryIn, CarryOut);
  Multiplexer #(.select(4), .width(32)) multiplexer_1 (
    .in0(OUTPUT), .in3(or_1_out), .in5(and_1_out), .in6(n32_bit_adder_subtractor_1_output),
    .in8(n32_bit_adder_subtractor_1_output), .in13(comparator_1_eq), .in14(comparator_1_gt),
    .in15(comparator_1_lt), .out(multiplexer_1_out), .sel(OpCode));  // open: in1, in2, in4, in7, in9, in10, in11, in12, en
  Register #(.width(32)) ACC (.D(multiplexer_1_out), .Q(OUTPUT), .clk(clk), .clr(clr));  // open: en
endmodule
